# Fritzing sketch SparkFun_SEN-12064_HTU21D_Breakout (saved by Fritzing 0.8.3b)
breadboards: 1

parts:
  Part1 = HTU21D Breakout
  Part2 = Arduino Uno (Rev3)
  R3 = Resistor [tolerance=±5% resistance=10k package="0603 [SMD]"]
  R4 = Resistor [tolerance=±5% resistance=10k package="0603 [SMD]"]

nets:
  N1: Part1.SCL, R4.Pin_0
  N2: Part1.SDA, R3.Pin_0
  GND: Part1.GND, Part2.GND
  3.3V: Part1.3.3V, Part2.3V3
  N3: Part2.A4/SDA, R3.Pin_1
  N4: Part2.A5/SCL, R4.Pin_1

custom parts:
  HTU21D Breakout: This is a breadboard friendly breakout board for the Measurement Specialties high-precision, low-power digital humidity sensor.
