# Fritzing sketch SparkFun_T5400_Frtizing_Diagram (saved by Fritzing 0.8.7b)

parts:
  RedBoard1 = RedBoard [part_number=DEV-11575]
  Part1 = SparkFun T5403 Barometer Breakout

nets:
  3V3: RedBoard1.3V3, Part1.VCC
  GND: RedBoard1.GND, Part1.GND
  N1: RedBoard1.A4, Part1.SDA/MOSI
  N2: RedBoard1.A5, Part1.SCL/SCLK

custom parts:
  RedBoard: At SparkFun we use many Arduinos and we're always looking for the simplest, most stable one. Each board is a bit different and no one board has everything we want, so we decided to make our own version that combines all our favorite features. The RedBoard combines the simplicity of the UNO's Optiboot bootloader (which is used in the Pro series), the stability of the FTDI (which we all missed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
  SparkFun T5403 Barometer Breakout: A breakout for the SparkFun T5403 Barometer.
