# Fritzing sketch sik_redboard_circuit_01 (saved by Fritzing 0.9.3b)
breadboards: 1

parts:
  LED1 = LED - 5mm [color="Yellow (592nm)" package="5 mm [THT]"]
  R1 = Resistor [tolerance=±10% resistance=330 package=THT]
  Parts1 = SparkFun RedBoard [part_number=DEV-12757]

nets:
  N1: LED1.cathode, R1.Pin_0
  N2: LED1.anode, Parts1.D13/SCK
  N3: R1.Pin_1, Parts1.GND

custom parts:
  SparkFun RedBoard: At SparkFun we use many Arduinos and we’re always looking for the simplest, most stable one. Each board is a bit different and no one board has everything we want, so we decided to make our own version that combines all our favorite features. The RedBoard combines the simplicity of the UNO’s Optiboot bootloader (which is used in the Pro series), the stability of the FTDI (which we all missed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
