# Fritzing sketch sik_redboard_circuit_02 (saved by Fritzing 0.9.3b)
breadboards: 1

parts:
  R8 = TSR-3386UT Square Trimming Potentiometer [part_number=TSR-3386]
  LED1 = LED - 5mm [color="Yellow (585nm)" package="5 mm [THT]"]
  R9 = Resistor [tolerance=±5% resistance=330 package=THT]
  Parts1 = SparkFun RedBoard [part_number=DEV-12757]

nets:
  N1: R8.Leg1, Parts1.5V
  N2: R8.wiper, Parts1.A0
  N3: R8.Leg2, R9.Pin_1, Parts1.GND
  N4: LED1.cathode, R9.Pin_0
  N5: LED1.anode, Parts1.D13/SCK

custom parts:
  TSR-3386UT Square Trimming Potentiometer: Trimpot 10K with Knob
  SparkFun RedBoard: At SparkFun we use many Arduinos and we’re always looking for the simplest, most stable one. Each board is a bit different and no one board has everything we want, so we decided to make our own version that combines all our favorite features. The RedBoard combines the simplicity of the UNO’s Optiboot bootloader (which is used in the Pro series), the stability of the FTDI (which we all missed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
