# Fritzing sketch sik_redboard_circuit_03 (saved by Fritzing 0.9.3b)
breadboards: 1

parts:
  LED1 = RGB LED - (4 legs) [package="5 mm [THT]"]
  R1 = Resistor [tolerance=±5% resistance=330 package=THT]
  R2 = Resistor [tolerance=±5% resistance=330 package=THT]
  R3 = Resistor [tolerance=±5% resistance=330 package=THT]
  Parts1 = SparkFun RedBoard [part_number=DEV-12757]

nets:
  N1: LED1.red_cathode, R1.Pin_1
  N2: LED1.common_anode, Parts1.GND
  N3: LED1.green_cathode, R2.Pin_1
  N4: LED1.blue_cathode, R3.Pin_1
  N5: R1.Pin_0, Parts1.D9_PWM
  N6: R2.Pin_0, Parts1.D10_PWM/SS
  N7: R3.Pin_0, Parts1.D11_PWM/MOSI

custom parts:
  SparkFun RedBoard: At SparkFun we use many Arduinos and we’re always looking for the simplest, most stable one. Each board is a bit different and no one board has everything we want, so we decided to make our own version that combines all our favorite features. The RedBoard combines the simplicity of the UNO’s Optiboot bootloader (which is used in the Pro series), the stability of the FTDI (which we all missed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
