# Fritzing sketch sik_redboard_circuit_05 (saved by Fritzing 0.9.0b)
breadboards: 1

parts:
  R7 = Resistor [tolerance=±5% resistance=10k package=THT]
  R8 = Resistor [tolerance=±5% resistance=330 package=THT]
  R9 = Resistor [tolerance=±5% resistance=10k package=THT]
  LED1 = LED - 5mm [color="Red (633nm)" package="5 mm [THT]"]
  S1 = SWITCH-MOMENTARY-2 [package=tactile-pth-12mm]
  S2 = SWITCH-MOMENTARY-2 [package=tactile-pth-12mm]
  Parts1 = SparkFun RedBoard [part_number=DEV-12757]

nets:
  N1: R7.Pin_0, S2.pin_4, Parts1.D3_PWM
  N2: R7.Pin_1, R9.Pin_1, Parts1.5V
  N3: R8.Pin_0, LED1.cathode
  N4: R8.Pin_1, S1.pin_3, S2.pin_3, Parts1.GND
  N5: R9.Pin_0, S1.pin_4, Parts1.D2
  N6: LED1.anode, Parts1.D13/SCK

custom parts:
  SWITCH-MOMENTARY-2: Various NO switches- pushbuttons, reed, etc
  SparkFun RedBoard: At SparkFun we use many Arduinos and we’re always looking for the simplest, most stable one. Each board is a bit different and no one board has everything we want, so we decided to make our own version that combines all our favorite features. The RedBoard combines the simplicity of the UNO’s Optiboot bootloader (which is used in the Pro series), the stability of the FTDI (which we all missed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
