# Fritzing sketch sik_redboard_circuit_06 (saved by Fritzing 0.9.0b)
breadboards: 1

parts:
  R7 = Resistor [tolerance=±5% resistance=10k package=THT]
  LED1 = LED - 5mm [color="Yellow (592nm)" package="5 mm [THT]"]
  R8 = Resistor [tolerance=±5% resistance=330 package=THT]
  R10 = Photocell (LDR) [package=THT]
  Parts1 = SparkFun RedBoard [part_number=DEV-12757]

nets:
  N1: R7.Pin_0, R10.pin_1, Parts1.A0
  N2: R7.Pin_1, R8.Pin_1, Parts1.GND
  N3: LED1.cathode, R8.Pin_0
  N4: LED1.anode, Parts1.D9_PWM
  N5: R10.pin_0, Parts1.5V

custom parts:
  SparkFun RedBoard: At SparkFun we use many Arduinos and we’re always looking for the simplest, most stable one. Each board is a bit different and no one board has everything we want, so we decided to make our own version that combines all our favorite features. The RedBoard combines the simplicity of the UNO’s Optiboot bootloader (which is used in the Pro series), the stability of the FTDI (which we all missed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
