# Fritzing sketch sik_redboard_circuit_13 (saved by Fritzing 0.9.0b)
breadboards: 1

parts:
  Q1 = NPN-Transistor [package="TO92 [THT]"]
  U2 = DIODE-ZENER [package=diode-zener]
  R1 = Resistor [tolerance=±5% resistance=330 package=THT]
  LED2 = LED - 5mm [color="Yellow (592nm)" package="5 mm [THT]"]
  LED3 = LED - 5mm [color="Red (633nm)" package="5 mm [THT]"]
  R2 = Resistor [tolerance=±5% resistance=330 package=THT]
  U3 = RELAY [package=relay-g5q]
  Parts1 = SparkFun RedBoard [part_number=DEV-12757]

nets:
  N1: Q1.E, U2.A, U3.COIL2
  N2: Q1.B, LED2.cathode, LED3.cathode, Parts1.GND
  N3: Q1.C, R1.Pin_0
  N4: U2.C, R2.Pin_0, U3.COIL1, Parts1.5V
  N5: R1.Pin_1, Parts1.D2
  N6: LED3.anode, U3.MAIN
  N7: R2.Pin_1, U3.NC

custom parts:
  DIODE-ZENER: Zener Diode Production Part - 8199 3.4V Zener Voltage
  RELAY: SPDT relay (COM-00100)
  SparkFun RedBoard: At SparkFun we use many Arduinos and we’re always looking for the simplest, most stable one. Each board is a bit different and no one board has everything we want, so we decided to make our own version that combines all our favorite features. The RedBoard combines the simplicity of the UNO’s Optiboot bootloader (which is used in the Pro series), the stability of the FTDI (which we all missed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
