# Fritzing sketch sik_redboard_circuit_14 (saved by Fritzing 0.9.0b)
breadboards: 1

parts:
  R1 = Resistor [tolerance=±5% resistance=330 package=THT]
  LED2 = LED - 5mm [color="Yellow (592nm)" package="5 mm [THT]"]
  LED3 = LED - 5mm [color="Red (633nm)" package="5 mm [THT]"]
  LED4 = LED - 5mm [color="Yellow (592nm)" package="5 mm [THT]"]
  U1 = 74HC595 SMD [package="SO16 [SMD]"]
  LED5 = LED - 5mm [color="Yellow (592nm)" package="5 mm [THT]"]
  LED6 = LED - 5mm [color="Yellow (592nm)" package="5 mm [THT]"]
  LED7 = LED - 5mm [color="Red (633nm)" package="5 mm [THT]"]
  LED8 = LED - 5mm [color="Red (633nm)" package="5 mm [THT]"]
  LED9 = LED - 5mm [color="Red (633nm)" package="5 mm [THT]"]
  R3 = Resistor [tolerance=±5% resistance=330 package=THT]
  R4 = Resistor [tolerance=±5% resistance=330 package=THT]
  R5 = Resistor [tolerance=±5% resistance=330 package=THT]
  R6 = Resistor [tolerance=±5% resistance=330 package=THT]
  R7 = Resistor [tolerance=±5% resistance=330 package=THT]
  R8 = Resistor [tolerance=±5% resistance=330 package=THT]
  R9 = Resistor [tolerance=±5% resistance=330 package=THT]
  Parts1 = SparkFun RedBoard [part_number=DEV-12757]

nets:
  N1: R1.Pin_0, LED6.cathode
  GND: R1.Pin_1, U1.GND, U1.OE, R3.Pin_1, R4.Pin_1, R5.Pin_1, R6.Pin_0, R7.Pin_0, R8.Pin_0, R9.Pin_0, Parts1.GND
  N2: LED2.cathode, R5.Pin_0
  N3: LED2.anode, U1.Q4
  N4: LED3.cathode, R6.Pin_1
  N5: LED3.anode, U1.Q3
  N6: LED4.cathode, R3.Pin_0
  N7: LED4.anode, U1.Q5
  N8: U1.Q1, LED8.anode
  N9: U1.Q2, LED7.anode
  N10: U1.Q6, LED5.anode
  N11: U1.Q7, LED6.anode
  VCC: U1.MR, U1.VCC, Parts1.5V
  N12: U1.SH_CP, Parts1.D3_PWM
  N13: U1.ST_CP, Parts1.D4
  N14: U1.DS, Parts1.D2
  N15: U1.Q0, LED9.anode
  N16: LED5.cathode, R4.Pin_0
  N17: LED7.cathode, R7.Pin_1
  N18: LED8.cathode, R8.Pin_1
  N19: LED9.cathode, R9.Pin_1

custom parts:
  SparkFun RedBoard: At SparkFun we use many Arduinos and we’re always looking for the simplest, most stable one. Each board is a bit different and no one board has everything we want, so we decided to make our own version that combines all our favorite features. The RedBoard combines the simplicity of the UNO’s Optiboot bootloader (which is used in the Pro series), the stability of the FTDI (which we all missed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
