# Fritzing sketch sik_arduino_circuit_02 (saved by Fritzing 0.9.0b)
breadboards: 1

parts:
  R8 = TSR-3386UT Square Trimming Potentiometer [part_number=TSR-3386]
  LED1 = LED - 5mm [color="Yellow (585nm)" package="5 mm [THT]"]
  R9 = Resistor [tolerance=±5% resistance=330 package=THT]
  Part1 = Arduino Uno (Rev3)

nets:
  N1: R8.Leg1, Part1.5V
  N2: R8.wiper, Part1.A0
  N3: R8.Leg2, R9.Pin_1, Part1.GND
  N4: LED1.cathode, R9.Pin_0
  N5: LED1.anode, Part1.D13/SCK

custom parts:
  TSR-3386UT Square Trimming Potentiometer: Trimpot 10K with Knob
