# Fritzing sketch sik_arduino_circuit_09 (saved by Fritzing 0.9.0b)
breadboards: 1

parts:
  J1 = Basic Servo
  R1 = Basic Flex Resistor
  R2 = Resistor [tolerance=±5% resistance=10k package=THT]
  Part1 = Arduino Uno (Rev3)

nets:
  GND: J1.gnd, R1.pin_1, Part1.GND
  VCC: J1.vcc, R2.Pin_1, Part1.5V
  N1: J1.pulse, Part1.D9_PWM
  N2: R1.Pin_2, R2.Pin_0, Part1.A0
