# Fritzing sketch sik_arduino_circuit_11 (saved by Fritzing 0.9.0b)
breadboards: 1

parts:
  SG3 = Buzzer 12mm [package=buzzer-12mm-ns]
  Part1 = Arduino Uno (Rev3)

nets:
  N1: SG3.1, Part1.D9_PWM
  N2: SG3.2, Part1.GND

custom parts:
  Buzzer 12mm: Buzzer 12mm Spark Fun Electronics SKU : Comp-Buzzer Through hole
