# Fritzing sketch sik_arduino_circuit_12 (saved by Fritzing 0.9.0b)
breadboards: 1

parts:
  Q1 = NPN-Transistor [package="TO92 [THT]"]
  U2 = DIODE-ZENER [package=diode-zener]
  R1 = Resistor [tolerance=±5% resistance=330 package=THT]
  M1 = DC Motor
  Part1 = Arduino Uno (Rev3)

nets:
  N1: Q1.E, U2.A, M1.pin_2
  N2: Q1.B, Part1.GND
  N3: Q1.C, R1.Pin_0
  N4: U2.C, M1.pin_1, Part1.5V
  N5: R1.Pin_1, Part1.D9_PWM

custom parts:
  DIODE-ZENER: Zener Diode Production Part - 8199 3.4V Zener Voltage
