# Fritzing sketch sik_arduino_circuit_15 (saved by Fritzing 0.9.0b)
breadboards: 1

parts:
  R8 = TSR-3386UT Square Trimming Potentiometer [part_number=TSR-3386]
  LCD1 = LCD screen
  Part1 = Arduino Uno (Rev3)

nets:
  VSS: R8.Leg1, LCD1.VSS, LCD1.R/W, LCD1.LED-, Part1.GND
  N1: R8.wiper, LCD1.V0
  VDD: R8.Leg2, LCD1.VDD, LCD1.LED+, Part1.5V
  N2: LCD1.RS, Part1.D12/MISO
  N3: LCD1.E, Part1.D11_PWM/MOSI
  N4: LCD1.DB4, Part1.D5_PWM
  N5: LCD1.DB5, Part1.D4
  N6: LCD1.DB6, Part1.D3_PWM
  N7: LCD1.DB7, Part1.D2

custom parts:
  TSR-3386UT Square Trimming Potentiometer: Trimpot 10K with Knob
  LCD screen: A standard character display, usually with 2x16 characters. Comes in many colors.
