# Fritzing sketch sik_arduino_circuit_16 (saved by Fritzing 0.9.0b)
breadboards: 1

parts:
  R1 = Resistor [tolerance=±5% resistance=330 package=THT]
  R5 = Resistor [tolerance=±5% resistance=330 package=THT]
  S1 = SWITCH-MOMENTARY-2 [package=tactile-pth-12mm]
  S2 = SWITCH-MOMENTARY-2 [package=tactile-pth-12mm]
  S3 = SWITCH-MOMENTARY-2 [package=tactile-pth-12mm]
  S4 = SWITCH-MOMENTARY-2 [package=tactile-pth-12mm]
  SG1 = Buzzer 12mm [package=buzzer-12mm-ns]
  R6 = Resistor [tolerance=±5% resistance=330 package=THT]
  R7 = Resistor [tolerance=±5% resistance=330 package=THT]
  LED1 = LED - 5mm [color="Yellow (592nm)" package="5 mm [THT]"]
  LED2 = LED - 5mm [color="Blue (505nm)" package="5 mm [THT]"]
  LED3 = LED - 5mm [color="Green (560nm)" package="5 mm [THT]"]
  LED4 = LED - 5mm [color="Red (635nm)" package="5 mm [THT]"]
  Part1 = Arduino Uno (Rev3)

nets:
  N1: R1.Pin_0, Part1.D5_PWM
  N2: R1.Pin_1, LED1.anode
  N3: R5.Pin_0, Part1.D3_PWM
  N4: R5.Pin_1, LED3.anode
  N5: S1.1, S2.1, S3.1, S4.1, LED1.cathode, LED2.cathode, LED3.cathode, LED4.cathode, Part1.GND
  N6: S1.2, Part1.D6_PWM
  N7: S2.2, Part1.D12/MISO
  N8: S3.2, Part1.D9_PWM
  N9: S4.2, Part1.D2
  N10: SG1.1, Part1.D4
  N11: SG1.2, Part1.D7
  N12: R6.Pin_0, Part1.D13/SCK
  N13: R6.Pin_1, LED2.anode
  N14: R7.Pin_0, Part1.D10_PWM/SS
  N15: R7.Pin_1, LED4.anode

custom parts:
  SWITCH-MOMENTARY-2: Various NO switches- pushbuttons, reed, etc
  Buzzer 12mm: Buzzer 12mm Spark Fun Electronics SKU : Comp-Buzzer Through hole
