# Fritzing sketch MicroViewInventorsKit_Circuit01 (saved by Fritzing 0.9.3b)
breadboards: 1

parts:
  MVPROG1 = MicroView with Programmer [part_number=MicroView package="16pin wide"]
  R1 = Resistor [tolerance=±5% resistance=330 package=THT]
  LED1 = LED - 5mm [color="Red (633nm)" package="5 mm [THT]"]

nets:
  N1: MVPROG1.A3, R1.Pin_0
  N2: MVPROG1.GND, LED1.cathode
  N3: R1.Pin_1, LED1.anode

custom parts:
  MicroView with Programmer: MicroView - Chip-sized Arduino with OLED display.
