# Fritzing sketch MicroViewInventorsKit_Circuit03 (saved by Fritzing 0.9.3b)
breadboards: 1

parts:
  MVPROG1 = MicroView with Programmer [part_number=MicroView package="16pin wide"]
  LED1 = RGB LED - (4 legs) [package="5 mm [THT]"]
  R3 = Resistor [tolerance=±5% resistance=330 package="2010 [SMD]"]
  R4 = Resistor [tolerance=±5% resistance=330 package="2010 [SMD]"]
  R5 = Resistor [tolerance=±5% resistance=330 package="2010 [SMD]"]

nets:
  N1: MVPROG1.GND, LED1.common_anode
  N2: MVPROG1.D3, R3.Pin_0
  N3: MVPROG1.D5, R5.Pin_0
  N4: MVPROG1.D6, R4.Pin_0
  N5: LED1.red_cathode, R4.Pin_1
  N6: LED1.green_cathode, R5.Pin_1
  N7: LED1.blue_cathode, R3.Pin_1

custom parts:
  MicroView with Programmer: MicroView - Chip-sized Arduino with OLED display.
