# Fritzing sketch MicroViewInventorsKit_Circuit04 (saved by Fritzing 0.9.3b)
breadboards: 1

parts:
  MVPROG1 = MicroView with Programmer [part_number=MicroView package="16pin wide"]
  S2 = SWITCH-MOMENTARY-2 [package=tactile-pth-12mm]

nets:
  N1: MVPROG1.A0, S2.pin_3
  N2: MVPROG1.GND, S2.pin_4

custom parts:
  MicroView with Programmer: MicroView - Chip-sized Arduino with OLED display.
  SWITCH-MOMENTARY-2: Various NO switches- pushbuttons, reed, etc
