# Fritzing sketch MicroViewInventorsKit_Circuit05 (saved by Fritzing 0.9.3b)
breadboards: 1

parts:
  MVPROG2 = MicroViewProg [part_number=MicroView]
  R1 = PHOTOCELL [package=photocell-kit]

nets:
  N1: MVPROG2.connector4, R1.P$2
  N2: MVPROG2.connector7, R1.P$1
