# Fritzing sketch MicroViewInventorsKit_Circuit06 (saved by Fritzing 0.9.3b)
breadboards: 1

parts:
  MVPROG2 = MicroViewProg [part_number=MicroView]
  T1 = TMP36 Temperature Sensor [package="TO92 [THT]"]

nets:
  N1: MVPROG2.connector6, T1.Vout
  N2: MVPROG2.connector7, T1.GND
  N3: MVPROG2.connector14, T1.+Vs
