# Fritzing sketch MicroViewInventorsKit_Circuit07 (saved by Fritzing 0.9.3b)
breadboards: 1

parts:
  MVPROG2 = MicroViewProg [part_number=MicroView]
  J1 = Basic Servo

nets:
  N1: MVPROG2.connector7, J1.gnd
  N2: MVPROG2.connector14, J1.vcc
