# Fritzing sketch MicroViewInventorsKit_Circuit08 (saved by Fritzing 0.9.3b)
breadboards: 1

parts:
  MVPROG2 = MicroViewProg [part_number=MicroView]
  SG4 = Buzzer 12mm [package=buzzer-12mm-ns]

nets:
  N1: MVPROG2.connector6, SG4.1
  N2: MVPROG2.connector7, SG4.2

custom parts:
  Buzzer 12mm: Buzzer 12mm Spark Fun Electronics SKU : Comp-Buzzer Through hole
