# Fritzing sketch MicroViewInventorsKit_Circuit09 (saved by Fritzing 0.9.3b)
breadboards: 1

parts:
  MVPROG2 = MicroViewProg [part_number=MicroView]
  Q1 = TRANSISTOR_NPN [package=to-92-ammo]
  U3 = DIODE-ZENER [package=diode-zener]
  M1 = DC Motor
  R1 = Resistor [tolerance=±5% resistance=330 package="0402 [SMD]"]

nets:
  N1: MVPROG2.connector7, Q1.C
  N2: MVPROG2.connector11, R1.Pin_0
  N3: MVPROG2.connector14, U3.C, M1.pin_1
  N4: Q1.E, U3.A, M1.pin_2
  N5: Q1.B, R1.Pin_1

custom parts:
  DIODE-ZENER: Zener Diode Production Part - 8199 3.4V Zener Voltage
