# Fritzing sketch MicroViewInventorsKit_Circuit10 (saved by Fritzing 0.9.3b)
breadboards: 1

parts:
  MVPROG2 = MicroViewProg [part_number=MicroView]
  Q1 = TRANSISTOR_NPN [package=to-92-ammo]
  U3 = DIODE-ZENER [package=diode-zener]
  R1 = Resistor [tolerance=±5% resistance=330 package="0402 [SMD]"]
  U6 = RELAY [package=relay-g5q]
  R2 = Resistor [tolerance=±5% resistance=330 package="0402 [SMD]"]
  LED1 = smd LED [color="Yellow (592nm)" package="1206 [SMD]"]
  LED2 = smd LED [color="Red (635nm)" package="1206 [SMD]"]

nets:
  N1: MVPROG2.connector7, Q1.C, LED1.cathode, LED2.cathode
  N2: MVPROG2.connector10, R1.Pin_0
  N3: MVPROG2.connector14, U3.C, U6.COIL1, R2.Pin_1
  N4: Q1.E, U3.A, U6.COIL2
  N5: Q1.B, R1.Pin_1
  N6: U6.MAIN, LED2.anode
  N7: U6.NO, LED1.anode
  N8: U6.NC, R2.Pin_0

custom parts:
  DIODE-ZENER: Zener Diode Production Part - 8199 3.4V Zener Voltage
  RELAY: SPDT relay (COM-00100)
