# Fritzing sketch MicroViewInventorsKit_Circuit11 (saved by Fritzing 0.9.3b)
breadboards: 1

parts:
  MVPROG2 = MicroViewProg [part_number=MicroView]
  R2 = Resistor [tolerance=±5% resistance=330 package="0402 [SMD]"]
  R1 = Resistor [tolerance=±5% resistance=330 package="0402 [SMD]"]
  R4 = SoftPot Potentiometer 200mm

nets:
  N1: MVPROG2.connector6, R2.Pin_1
  N2: MVPROG2.connector7, R4.leg2
  N3: MVPROG2.connector14, R1.Pin_1
  N4: R2.Pin_0, R4.wiper
  N5: R1.Pin_0, R4.leg1

custom parts:
  SoftPot Potentiometer 200mm: These are very thin variable potentiometers. By pressing down on various parts of the strip, the resistance linearly changes from 100Ohms to 10,000Ohms allowing the user to very accurately calculate the relative position on the strip. Can be used as an accurate positional indicator for CNC head positioning, variable user input (volume level input for example), straight user input (multiple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
