# Fritzing sketch sik_redboard_circuit_04 (saved by Fritzing 0.9.3b)
breadboards: 1

parts:
  R1 = Resistor [tolerance=±5% resistance=330 package=THT]
  R2 = Resistor [tolerance=±5% resistance=330 package=THT]
  R3 = Resistor [tolerance=±5% resistance=330 package=THT]
  R4 = Resistor [tolerance=±5% resistance=330 package=THT]
  LED5 = LED - 5mm [color="Red (635nm)" package="5 mm [THT]"]
  R5 = Resistor [tolerance=±5% resistance=330 package=THT]
  LED6 = LED - 5mm [color="Red (635nm)" package="5 mm [THT]"]
  R6 = Resistor [tolerance=±5% resistance=330 package=THT]
  LED7 = LED - 5mm [color="Red (635nm)" package="5 mm [THT]"]
  LED8 = LED - 5mm [color="Red (635nm)" package="5 mm [THT]"]
  R7 = Resistor [tolerance=±5% resistance=330 package=THT]
  R8 = Resistor [tolerance=±5% resistance=330 package=THT]
  LED4 = LED - 5mm [color="Yellow (595nm)" package="5 mm [THT]"]
  LED3 = LED - 5mm [color="Yellow (595nm)" package="5 mm [THT]"]
  LED2 = LED - 5mm [color="Yellow (595nm)" package="5 mm [THT]"]
  LED1 = LED - 5mm [color="Yellow (595nm)" package="5 mm [THT]"]
  Parts1 = SparkFun RedBoard [part_number=DEV-12757]

nets:
  N1: R1.Pin_0, LED1.cathode
  N2: R1.Pin_1, R2.Pin_1, R3.Pin_1, R4.Pin_1, R5.Pin_1, R6.Pin_1, R7.Pin_1, R8.Pin_1, Parts1.GND
  N3: R2.Pin_0, LED2.cathode
  N4: R3.Pin_0, LED3.cathode
  N5: R4.Pin_0, LED4.cathode
  N6: LED5.cathode, R5.Pin_0
  N7: LED5.anode, Parts1.D6_PWM
  N8: LED6.cathode, R6.Pin_0
  N9: LED6.anode, Parts1.D7
  N10: LED7.cathode, R7.Pin_0
  N11: LED7.anode, Parts1.D8
  N12: LED8.cathode, R8.Pin_0
  N13: LED8.anode, Parts1.D9_PWM
  N14: LED4.anode, Parts1.D5_PWM
  N15: LED3.anode, Parts1.D4
  N16: LED2.anode, Parts1.D3_PWM
  N17: LED1.anode, Parts1.D2

custom parts:
  SparkFun RedBoard: At SparkFun we use many Arduinos and we’re always looking for the simplest, most stable one. Each board is a bit different and no one board has everything we want, so we decided to make our own version that combines all our favorite features. The RedBoard combines the simplicity of the UNO’s Optiboot bootloader (which is used in the Pro series), the stability of the FTDI (which we all missed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
