# Fritzing sketch sik_redboard_circuit_07 (saved by Fritzing 0.9.3b)
breadboards: 1

parts:
  U1 = TMP36 [package=to-92-kit]
  Parts1 = SparkFun RedBoard [part_number=DEV-12757]

nets:
  VCC: U1.VCC, Parts1.5V
  N1: U1.VOUT, Parts1.A0
  GND: U1.GND, Parts1.GND

custom parts:
  SparkFun RedBoard: At SparkFun we use many Arduinos and we’re always looking for the simplest, most stable one. Each board is a bit different and no one board has everything we want, so we decided to make our own version that combines all our favorite features. The RedBoard combines the simplicity of the UNO’s Optiboot bootloader (which is used in the Pro series), the stability of the FTDI (which we all missed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
