# Fritzing sketch sik_redboard_circuit_11 (saved by Fritzing 0.9.0b)
breadboards: 1

parts:
  SG3 = Buzzer 12mm [package=buzzer-12mm-ns]
  Parts1 = SparkFun RedBoard [part_number=DEV-12757]

nets:
  N1: SG3.1, Parts1.D9_PWM
  N2: SG3.2, Parts1.GND

custom parts:
  Buzzer 12mm: Buzzer 12mm Spark Fun Electronics SKU : Comp-Buzzer Through hole
  SparkFun RedBoard: At SparkFun we use many Arduinos and we’re always looking for the simplest, most stable one. Each board is a bit different and no one board has everything we want, so we decided to make our own version that combines all our favorite features. The RedBoard combines the simplicity of the UNO’s Optiboot bootloader (which is used in the Pro series), the stability of the FTDI (which we all missed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
