# Fritzing sketch sik_redboard_circuit_12 (saved by Fritzing 0.9.3b)
breadboards: 1

parts:
  U2 = DIODE-ZENER [package=diode-zener]
  R1 = Resistor [tolerance=±5% resistance=330 package=THT]
  M1 = DC Motor
  Parts1 = SparkFun RedBoard [part_number=DEV-12757]
  Q2 = NPN-Transistor [package="TO92 [THT]"]

nets:
  N1: U2.C, M1.pin_1, Parts1.5V
  N2: U2.A, M1.pin_2, Q2.E
  N3: R1.Pin_0, Q2.C
  N4: R1.Pin_1, Parts1.D9_PWM
  N5: Parts1.GND, Q2.B

custom parts:
  DIODE-ZENER: Zener Diode Production Part - 8199 3.4V Zener Voltage
  SparkFun RedBoard: At SparkFun we use many Arduinos and we’re always looking for the simplest, most stable one. Each board is a bit different and no one board has everything we want, so we decided to make our own version that combines all our favorite features. The RedBoard combines the simplicity of the UNO’s Optiboot bootloader (which is used in the Pro series), the stability of the FTDI (which we all missed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
  NPN-Transistor: A standard NPN-transistor
