# Fritzing sketch sik_redboard_circuit_15 (saved by Fritzing 0.9.3b)
breadboards: 1

parts:
  R8 = TSR-3386UT Square Trimming Potentiometer [part_number=TSR-3386]
  LCD1 = LCD screen
  Parts1 = SparkFun RedBoard [part_number=DEV-12757]

nets:
  VSS: R8.Leg1, LCD1.VSS, LCD1.R/W, LCD1.LED-, Parts1.GND
  N1: R8.wiper, LCD1.V0
  VDD: R8.Leg2, LCD1.VDD, LCD1.LED+, Parts1.5V
  N2: LCD1.RS, Parts1.D12/MISO
  N3: LCD1.E, Parts1.D11_PWM/MOSI
  N4: LCD1.DB4, Parts1.D5_PWM
  N5: LCD1.DB5, Parts1.D4
  N6: LCD1.DB6, Parts1.D3_PWM
  N7: LCD1.DB7, Parts1.D2

custom parts:
  TSR-3386UT Square Trimming Potentiometer: Trimpot 10K with Knob
  LCD screen: A standard character display, usually with 2x16 characters. Comes in many colors.
  SparkFun RedBoard: At SparkFun we use many Arduinos and we’re always looking for the simplest, most stable one. Each board is a bit different and no one board has everything we want, so we decided to make our own version that combines all our favorite features. The RedBoard combines the simplicity of the UNO’s Optiboot bootloader (which is used in the Pro series), the stability of the FTDI (which we all missed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
