# Fritzing sketch sik_arduino_circuit_03 (saved by Fritzing 0.9.3b)
breadboards: 1

parts:
  LED1 = RGB LED - (4 legs) [package="5 mm [THT]"]
  R1 = Resistor [tolerance=±5% resistance=330 package=THT]
  R2 = Resistor [tolerance=±5% resistance=330 package=THT]
  R3 = Resistor [tolerance=±5% resistance=330 package=THT]
  Part1 = Arduino Uno (Rev3)

nets:
  N1: LED1.red_cathode, R1.Pin_1
  N2: LED1.common_anode, Part1.GND
  N3: LED1.green_cathode, R2.Pin_1
  N4: LED1.blue_cathode, R3.Pin_1
  N5: R1.Pin_0, Part1.D9_PWM
  N6: R2.Pin_0, Part1.D10_PWM/SS
