# Fritzing sketch sik_arduino_circuit_05 (saved by Fritzing 0.9.3b)
breadboards: 1

parts:
  R7 = Resistor [tolerance=±5% resistance=10k package=THT]
  R8 = Resistor [tolerance=±5% resistance=330 package=THT]
  R9 = Resistor [tolerance=±5% resistance=10k package=THT]
  LED1 = LED - 5mm [color="Red (633nm)" package="5 mm [THT]"]
  S1 = SWITCH-MOMENTARY-2 [package=tactile-pth-12mm]
  S2 = SWITCH-MOMENTARY-2 [package=tactile-pth-12mm]
  Part1 = Arduino Uno (Rev3)  # not connected

nets:
  N1: R7.Pin_0, S2.pin_4
  N2: R7.Pin_1, R9.Pin_1
  N3: R8.Pin_0, LED1.cathode
  N4: R8.Pin_1, S1.pin_3, S2.pin_3
  N5: R9.Pin_0, S1.pin_4

custom parts:
  SWITCH-MOMENTARY-2: Various NO switches- pushbuttons, reed, etc
