# Fritzing sketch sik_arduino_circuit_06 (saved by Fritzing 0.9.3b)
breadboards: 1

parts:
  R7 = Resistor [tolerance=±5% resistance=10k package=THT]
  LED1 = LED - 5mm [color="Yellow (592nm)" package="5 mm [THT]"]
  R8 = Resistor [tolerance=±5% resistance=330 package=THT]
  R10 = Photocell (LDR) [package=THT]
  Part1 = Arduino Uno (Rev3)

nets:
  N1: R7.Pin_0, R10.pin_1, Part1.A0
  N2: R7.Pin_1, R8.Pin_1, Part1.GND
  N3: LED1.cathode, R8.Pin_0
  N4: LED1.anode, Part1.D9_PWM
  N5: R10.pin_0, Part1.5V
