# Fritzing sketch sik_arduino_circuit_09 (saved by Fritzing 0.9.3b)
breadboards: 1

parts:
  J1 = Basic Servo
  R2 = Resistor [tolerance=±5% resistance=10k package=THT]
  Part1 = Arduino Uno (Rev3)
  R4 = 2.2 inch Basic Flex Resistor

nets:
  GND: J1.gnd, Part1.GND, R4.Pin_2
  VCC: J1.vcc, R2.Pin_1, Part1.5V
  N1: J1.pulse, Part1.D9_PWM
  N2: R2.Pin_0, Part1.A0, R4.pin_1

custom parts:
  2.2 inch Basic Flex Resistor: A generic Flex resistor - SparkFun: SEN-10264
