# Fritzing sketch sik_arduino_circuit_10 (saved by Fritzing 0.9.3b)
breadboards: 1

parts:
  R2 = Resistor [tolerance=±5% resistance=10k package=THT]
  R3 = SoftPot Potentiometer 200mm
  LED1 = RGB LED - (4 legs) [package="5 mm [THT]"]
  R4 = Resistor [tolerance=±5% resistance=330 package=THT]
  R5 = Resistor [tolerance=±5% resistance=330 package=THT]
  R6 = Resistor [tolerance=±5% resistance=330 package=THT]
  Part1 = Arduino Uno (Rev3)

nets:
  N1: R2.Pin_0, R3.leg1, LED1.common_anode, Part1.GND
  N2: R2.Pin_1, R3.wiper, Part1.A0
  N3: R3.leg2, Part1.5V
  N4: LED1.red_cathode, R4.Pin_1
  N5: LED1.green_cathode, R5.Pin_1
  N6: LED1.blue_cathode, R6.Pin_1
  N7: R4.Pin_0, Part1.D9_PWM
  N8: R5.Pin_0, Part1.D10_PWM/SS
  N9: R6.Pin_0, Part1.D11_PWM/MOSI

custom parts:
  SoftPot Potentiometer 200mm: These are very thin variable potentiometers. By pressing down on various parts of the strip, the resistance linearly changes from 100Ohms to 10,000Ohms allowing the user to very accurately calculate the relative position on the strip. Can be used as an accurate positional indicator for CNC head positioning, variable user input (volume level input for example), straight user input (multiple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
