# Fritzing sketch sik_arduino_circuit_12 (saved by Fritzing 0.9.3b)
breadboards: 1

parts:
  U2 = DIODE-ZENER [package=diode-zener]
  R1 = Resistor [tolerance=±5% resistance=330 package=THT]
  M1 = DC Motor
  Part1 = Arduino Uno (Rev3)
  Q2 = NPN-Transistor [package="TO92 [THT]"]

nets:
  N1: U2.C, M1.pin_1, Part1.5V
  N2: U2.A, M1.pin_2, Q2.E
  N3: R1.Pin_0, Q2.C
  N4: R1.Pin_1, Part1.D9_PWM
  N5: Part1.GND, Q2.B

custom parts:
  DIODE-ZENER: Zener Diode Production Part - 8199 3.4V Zener Voltage
  NPN-Transistor: A standard NPN-transistor
