# Fritzing sketch sik_arduino_circuit_14 (saved by Fritzing 0.9.3b)
breadboards: 1

parts:
  U1 = 74HC595 SMD [package="SO16 [SMD]"]
  R11 = Resistor [tolerance=±5% resistance=330 package=THT]
  R12 = Resistor [tolerance=±5% resistance=330 package=THT]
  R13 = Resistor [tolerance=±5% resistance=330 package=THT]
  R14 = Resistor [tolerance=±5% resistance=330 package=THT]
  R17 = Resistor [tolerance=±5% resistance=330 package=THT]
  R18 = Resistor [tolerance=±5% resistance=330 package=THT]
  R19 = Resistor [tolerance=±5% resistance=330 package=THT]
  R20 = Resistor [tolerance=±5% resistance=330 package=THT]
  LED19 = LED from the top-view [part_number=COM-09594 package=PTH]
  LED20 = LED from the top-view [part_number=COM-09594 package=PTH]
  LED21 = LED from the top-view [part_number=COM-09594 package=PTH]
  LED22 = LED from the top-view [part_number=COM-09594 package=PTH]
  LED23 = LED from the top-view [part_number=COM-09594 package=PTH]
  LED24 = LED from the top-view [part_number=COM-09594 package=PTH]
  LED25 = LED from the top-view [part_number=COM-09594 package=PTH]
  LED26 = LED from the top-view [part_number=COM-09594 package=PTH]
  Part1 = Arduino Uno (Rev3)

nets:
  N1: U1.Q1, LED24.Anode_(+)
  N2: U1.Q2, LED25.Anode_(+)
  N3: U1.Q3, LED26.Anode_(+)
  N4: U1.Q4, LED19.Anode_(+)
  N5: U1.Q5, LED20.Anode_(+)
  N6: U1.Q6, LED21.Anode_(+)
  N7: U1.Q7, LED22.Anode_(+)
  GND: U1.GND, U1.OE, R11.Pin_0, R12.Pin_0, R13.Pin_0, R14.Pin_0, R17.Pin_1, R18.Pin_1, R19.Pin_1, R20.Pin_1, Part1.GND
  VCC: U1.MR, U1.VCC, Part1.5V
  N8: U1.SH_CP, Part1.D3_PWM
  N9: U1.ST_CP, Part1.D4
  N10: U1.DS, Part1.D2
  N11: U1.Q0, LED23.Anode_(+)
  N12: R11.Pin_1, LED25.Cathode_(-)
  N13: R12.Pin_1, LED26.Cathode_(-)
  N14: R13.Pin_1, LED24.Cathode_(-)
  N15: R14.Pin_1, LED23.Cathode_(-)
  N16: R17.Pin_0, LED19.Cathode_(-)
  N17: R18.Pin_0, LED20.Cathode_(-)
  N18: R19.Pin_0, LED21.Cathode_(-)
  N19: R20.Pin_0, LED22.Cathode_(-)

custom parts:
  LED from the top-view: A generic through-hole LED from the topview
  LED from the top-view: A generic through-hole LED from the topview
