# Fritzing sketch sik_arduino_circuit_16 (saved by Fritzing 0.9.3b)
breadboards: 1

parts:
  R1 = Resistor [tolerance=±5% resistance=330 package=THT]
  R5 = Resistor [tolerance=±5% resistance=330 package=THT]
  SG1 = Buzzer 12mm [package=buzzer-12mm-ns]
  R6 = Resistor [tolerance=±5% resistance=330 package=THT]
  R7 = Resistor [tolerance=±5% resistance=330 package=THT]
  LED1 = LED - 5mm [color="Yellow (592nm)" package="5 mm [THT]"]
  LED2 = LED - 5mm [color="Blue (505nm)" package="5 mm [THT]"]
  LED3 = LED - 5mm [color="Green (560nm)" package="5 mm [THT]"]
  LED4 = LED - 5mm [color="Red (635nm)" package="5 mm [THT]"]
  S5 = Pushbutton [package="[THT]"]
  S6 = Pushbutton [package="[THT]"]
  S7 = Pushbutton [package="[THT]"]
  S8 = Pushbutton [package="[THT]"]
  Part1 = Arduino Uno (Rev3)

nets:
  N1: R1.Pin_0, Part1.D5_PWM
  N2: R1.Pin_1, LED1.anode
  N3: R5.Pin_0, Part1.D3_PWM
  N4: R5.Pin_1, LED3.anode
  N5: SG1.1, Part1.D4
  N6: SG1.2, Part1.D7
  N7: R6.Pin_0, Part1.D13/SCK
  N8: R6.Pin_1, LED2.anode
  N9: R7.Pin_0, Part1.D10_PWM/SS
  N10: R7.Pin_1, LED4.anode
  N11: LED1.cathode, LED2.cathode, LED3.cathode, LED4.cathode, S5.Pin_1, S5.Pin_2, S6.Pin_1, S6.Pin_2, S7.Pin_1, S7.Pin_2, S8.Pin_1, S8.Pin_2, Part1.GND
  N12: S5.Pin_3, S5.Pin_4, Part1.D6_PWM
  N13: S6.Pin_3, S6.Pin_4, Part1.D9_PWM
  N14: S7.Pin_3, S7.Pin_4, Part1.D2
  N15: S8.Pin_3, S8.Pin_4, Part1.D12/MISO

custom parts:
  Buzzer 12mm: Buzzer 12mm Spark Fun Electronics SKU : Comp-Buzzer Through hole
  Pushbutton: A generic pushbutton.
  Pushbutton: A generic pushbutton.
  Pushbutton: A generic pushbutton.
  Pushbutton: A generic pushbutton.
