# Fritzing sketch SIK_Circuit_1B-Potentiometer (saved by Fritzing 0.9.3b)
breadboards: 1

parts:
  Parts1 = SparkFun RedBoard [part_number=DEV-12757]
  R1 = Resistor [tolerance=±5% resistance=330 package=THT]
  S1 = Flipped LED
  R10 = TSR-3386UT Square Trimming Potentiometer [part_number=TSR-3386]

nets:
  N1: Parts1.A0, R10.wiper
  N2: Parts1.D13/SCK, R1.Pin_1
  N3: Parts1.5V, R10.Leg2
  N4: Parts1.GND, S1.cathode, R10.Leg1
  N5: R1.Pin_0, S1.anode

custom parts:
  SparkFun RedBoard: At SparkFun we use many Arduinos and we’re always looking for the simplest, most stable one. Each board is a bit different and no one board has everything we want, so we decided to make our own version that combines all our favorite features. The RedBoard combines the simplicity of the UNO’s Optiboot bootloader (which is used in the Pro series), the stability of the FTDI (which we all missed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
  Flipped LED: Flipped version of the default LED
  TSR-3386UT Square Trimming Potentiometer: Trimpot 10K with Knob
