# Fritzing sketch SIK_Circuit_1D-Blink (saved by Fritzing 0.9.3b)
breadboards: 1

parts:
  Parts1 = SparkFun RedBoard [part_number=DEV-12757]
  R1 = Resistor [tolerance=±5% resistance=330 package=THT]
  R2 = PHOTOCELL [package=photocell-kit]
  R3 = Resistor [tolerance=±5% resistance=10k package=THT]
  R4 = Resistor [tolerance=±5% resistance=330 package=THT]
  R5 = Resistor [tolerance=±5% resistance=330 package=THT]
  R10 = TSR-3386UT Square Trimming Potentiometer [part_number=TSR-3386]
  LED1 = RGB LED (com. cathode, rgb) [package="5 mm [THT]"]

nets:
  N1: Parts1.A0, R2.P$1, R3.Pin_1
  N2: Parts1.A1, R10.wiper
  N3: Parts1.D9_PWM, R5.Pin_1
  N4: Parts1.D10_PWM/SS, R4.Pin_1
  N5: Parts1.D11_PWM/MOSI, R1.Pin_1
  N6: Parts1.5V, R2.P$2, R10.Leg2
  N7: Parts1.GND, R3.Pin_0, R10.Leg1, LED1.common_cathode
  N8: R1.Pin_0, LED1.blue_anode
  N9: R4.Pin_0, LED1.green_anode
  N10: R5.Pin_0, LED1.red_anode

custom parts:
  SparkFun RedBoard: At SparkFun we use many Arduinos and we’re always looking for the simplest, most stable one. Each board is a bit different and no one board has everything we want, so we decided to make our own version that combines all our favorite features. The RedBoard combines the simplicity of the UNO’s Optiboot bootloader (which is used in the Pro series), the stability of the FTDI (which we all missed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
  TSR-3386UT Square Trimming Potentiometer: Trimpot 10K with Knob
