# Fritzing sketch SIK_Circuit_2B_trumpet (saved by Fritzing 0.9.3b)
breadboards: 1

parts:
  Parts1 = SparkFun RedBoard [part_number=DEV-12757]
  SG4 = Buzzer 12mm [package=buzzer-12mm-ns]
  R9 = TSR-3386UT Square Trimming Potentiometer [part_number=TSR-3386]
  S6 = Pushbutton [part_number=COM-09190 package="[THT]"]
  S7 = Pushbutton [part_number=COM-09190 package="[THT]"]
  S8 = Pushbutton [part_number=COM-09190 package="[THT]"]

nets:
  N1: Parts1.D10_PWM/SS, SG4.1
  N2: Parts1.D2, S8.Pin_3, S8.Pin_4
  N3: Parts1.D3_PWM, S7.Pin_3, S7.Pin_4
  N4: Parts1.D4, S6.Pin_3, S6.Pin_4
  N5: Parts1.GND, R9.wiper, S6.Pin_1, S6.Pin_2, S7.Pin_1, S7.Pin_2, S8.Pin_1, S8.Pin_2
  N6: SG4.2, R9.Leg2

custom parts:
  SparkFun RedBoard: At SparkFun we use many Arduinos and we’re always looking for the simplest, most stable one. Each board is a bit different and no one board has everything we want, so we decided to make our own version that combines all our favorite features. The RedBoard combines the simplicity of the UNO’s Optiboot bootloader (which is used in the Pro series), the stability of the FTDI (which we all missed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
  Buzzer 12mm: Buzzer 12mm Spark Fun Electronics SKU : Comp-Buzzer Through hole
  TSR-3386UT Square Trimming Potentiometer: Trimpot 10K with Knob
  Pushbutton: A generic pushbutton. This is a standard 12mm square momentary button. What we really like is the large button head and good tactile feel (it ‘clicks’ really well). This button is great for user input on a PCB or a good, big reset button on a breadboard. Breadboard friendly! SparkFun Storefront SKU: COM-09190 Modified by: Ho Yun "Bobby" Chan @ SparkFun Electronics Inc.
