# Fritzing sketch SIK_Circuit_2B_w_Pullups (saved by Fritzing 0.9.3b)
breadboards: 1

parts:
  Parts1 = SparkFun RedBoard [part_number=DEV-12757]
  SG4 = Buzzer 12mm [package=buzzer-12mm-ns]
  R9 = TSR-3386UT Square Trimming Potentiometer [part_number=TSR-3386]
  S3 = SWITCH-MOMENTARY-2 [package=tactile-pth-12mm]
  S4 = SWITCH-MOMENTARY-2 [package=tactile-pth-12mm]
  S5 = SWITCH-MOMENTARY-2 [package=tactile-pth-12mm]
  R10 = Resistor [tolerance=±5% resistance=10k package=THT]
  R11 = Resistor [tolerance=±5% resistance=10k package=THT]
  R12 = Resistor [tolerance=±5% resistance=10k package=THT]

nets:
  N1: Parts1.D10_PWM/SS, SG4.1
  N2: Parts1.D2, S3.pin_4, R12.Pin_0
  N3: Parts1.D3_PWM, S4.pin_4, R11.Pin_0
  N4: Parts1.D4, S5.pin_4, R10.Pin_0
  N5: Parts1.GND, R9.wiper, S3.pin_3, S4.pin_3, S5.pin_3
  N6: SG4.2, R9.Leg2
  N7: R10.Pin_1, R11.Pin_1, R12.Pin_1

custom parts:
  SparkFun RedBoard: At SparkFun we use many Arduinos and we’re always looking for the simplest, most stable one. Each board is a bit different and no one board has everything we want, so we decided to make our own version that combines all our favorite features. The RedBoard combines the simplicity of the UNO’s Optiboot bootloader (which is used in the Pro series), the stability of the FTDI (which we all missed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
  Buzzer 12mm: Buzzer 12mm Spark Fun Electronics SKU : Comp-Buzzer Through hole
  TSR-3386UT Square Trimming Potentiometer: Trimpot 10K with Knob
  SWITCH-MOMENTARY-2: Various NO switches- pushbuttons, reed, etc
