# Fritzing sketch SIK_Circuit_2C_SimonSays (saved by Fritzing 0.9.3b)
breadboards: 1

parts:
  Parts1 = SparkFun RedBoard [part_number=DEV-12757]
  SG4 = Buzzer 12mm [package=buzzer-12mm-ns]
  R9 = TSR-3386UT Square Trimming Potentiometer [part_number=TSR-3386]
  LED1 = LED - 5mm [color="Blue (470nm)" package="5 mm [THT]"]
  LED3 = LED - 5mm [color="Yellow (595nm)" package="5 mm [THT]"]
  R10 = Resistor [tolerance=±5% resistance=330 package=THT]
  R11 = Resistor [tolerance=±5% resistance=330 package=THT]
  R12 = Resistor [tolerance=±5% resistance=330 package=THT]
  R13 = Resistor [tolerance=±5% resistance=330 package=THT]
  S7 = Pushbutton [part_number=COM-09190 package="[THT]"]
  S8 = Pushbutton [part_number=COM-09190 package="[THT]"]
  LED5 = LED - 5mm [color="Green (555nm)" package="5 mm [THT]"]
  S9 = Pushbutton [part_number=COM-09190 package="[THT]"]
  S10 = Pushbutton [part_number=COM-09190 package="[THT]"]
  LED6 = LED - 5mm [color="Red (633nm)" package="5 mm [THT]"]

nets:
  N1: Parts1.D8, S7.Pin_3, S7.Pin_4
  N2: Parts1.D9_PWM, LED1.anode
  N3: Parts1.D10_PWM/SS, SG4.1
  N4: Parts1.D2, S10.Pin_3, S10.Pin_4
  N5: Parts1.D3_PWM, LED6.anode
  N6: Parts1.D4, S9.Pin_3, S9.Pin_4
  N7: Parts1.D5_PWM, LED3.anode
  N8: Parts1.D6_PWM, S8.Pin_3, S8.Pin_4
  N9: Parts1.D7, LED5.anode
  N10: Parts1.GND, R9.wiper, R10.Pin_1, R11.Pin_1, R12.Pin_1, R13.Pin_1, S7.Pin_1, S7.Pin_2, S8.Pin_1, S8.Pin_2, S9.Pin_1, S9.Pin_2, S10.Pin_1, S10.Pin_2
  N11: SG4.2, R9.Leg2
  N12: LED1.cathode, R13.Pin_0
  N13: LED3.cathode, R11.Pin_0
  N14: R10.Pin_0, LED6.cathode
  N15: R12.Pin_0, LED5.cathode

custom parts:
  SparkFun RedBoard: At SparkFun we use many Arduinos and we’re always looking for the simplest, most stable one. Each board is a bit different and no one board has everything we want, so we decided to make our own version that combines all our favorite features. The RedBoard combines the simplicity of the UNO’s Optiboot bootloader (which is used in the Pro series), the stability of the FTDI (which we all missed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
  Buzzer 12mm: Buzzer 12mm Spark Fun Electronics SKU : Comp-Buzzer Through hole
  TSR-3386UT Square Trimming Potentiometer: Trimpot 10K with Knob
  Pushbutton: A generic pushbutton. This is a standard 12mm square momentary button. What we really like is the large button head and good tactile feel (it ‘clicks’ really well). This button is great for user input on a PCB or a good, big reset button on a breadboard. Breadboard friendly! SparkFun Storefront SKU: COM-09190 Modified by: Ho Yun "Bobby" Chan @ SparkFun Electronics Inc.
