# Fritzing sketch SIK_Circuit_3A_Servo_Motors (saved by Fritzing 0.9.3b)
breadboards: 1

parts:
  Parts1 = SparkFun RedBoard [part_number=DEV-12757]
  R9 = TSR-3386UT Square Trimming Potentiometer [part_number=TSR-3386]
  J2 = Basic Servo

nets:
  N1: Parts1.A0, R9.wiper
  N2: Parts1.D9_PWM, J2.pulse
  GND: Parts1.GND, R9.Leg1, J2.gnd
  5V: Parts1.5V, R9.Leg2, J2.vcc

custom parts:
  SparkFun RedBoard: At SparkFun we use many Arduinos and we’re always looking for the simplest, most stable one. Each board is a bit different and no one board has everything we want, so we decided to make our own version that combines all our favorite features. The RedBoard combines the simplicity of the UNO’s Optiboot bootloader (which is used in the Pro series), the stability of the FTDI (which we all missed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
  TSR-3386UT Square Trimming Potentiometer: Trimpot 10K with Knob
