# Fritzing sketch SIK_Circuit_3B_Distance_Sensor (saved by Fritzing 0.9.3b)
breadboards: 1

parts:
  Parts1 = SparkFun RedBoard [part_number=DEV-12757]
  R1 = Resistor [tolerance=±5% resistance=330 package=THT]
  R4 = Resistor [tolerance=±5% resistance=330 package=THT]
  R5 = Resistor [tolerance=±5% resistance=330 package=THT]
  LED1 = RGB LED (com. cathode, rgb) [package="5 mm [THT]"]
  hc-sr4 = hc-sr04

nets:
  N1: Parts1.D11_PWM/MOSI, hc-sr4.Trig
  N2: Parts1.D12/MISO, hc-sr4.Echo
  GND: Parts1.GND, LED1.common_cathode, hc-sr4.GND
  N3: Parts1.D3_PWM, R5.Pin_1
  N4: Parts1.D5_PWM, R4.Pin_1
  N5: Parts1.D6_PWM, R1.Pin_1
  5V: Parts1.5V, hc-sr4.VCC
  N6: R1.Pin_0, LED1.blue_anode
  N7: R4.Pin_0, LED1.green_anode
  N8: R5.Pin_0, LED1.red_anode

custom parts:
  SparkFun RedBoard: At SparkFun we use many Arduinos and we’re always looking for the simplest, most stable one. Each board is a bit different and no one board has everything we want, so we decided to make our own version that combines all our favorite features. The RedBoard combines the simplicity of the UNO’s Optiboot bootloader (which is used in the Pro series), the stability of the FTDI (which we all missed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
  hc-sr04: This is a HC-SR04 Distance Sensor
