# Fritzing sketch SIK_Circuit_4B_Temp_Sensor (saved by Fritzing 0.9.3b)
breadboards: 1

parts:
  Parts1 = SparkFun RedBoard [part_number=DEV-12757]
  LCD2 = LCD screen
  R3 = TSR-3386UT Square Trimming Potentiometer [part_number=TSR-3386]
  U2 = TMP36 [package=to-92-kit]

nets:
  N1: Parts1.A0, U2.VOUT
  N2: Parts1.D8, LCD2.DB7
  N3: Parts1.D9_PWM, LCD2.DB6
  N4: Parts1.D10_PWM/SS, LCD2.DB5
  N5: Parts1.D11_PWM/MOSI, LCD2.DB4
  N6: Parts1.D12/MISO, LCD2.E
  N7: Parts1.D13/SCK, LCD2.RS
  5V: Parts1.5V, LCD2.VDD, LCD2.LED+, R3.Leg1, U2.VCC
  GND: Parts1.GND, LCD2.VSS, LCD2.R/W, LCD2.LED-, R3.Leg2, U2.GND
  N8: LCD2.V0, R3.wiper

custom parts:
  SparkFun RedBoard: At SparkFun we use many Arduinos and we’re always looking for the simplest, most stable one. Each board is a bit different and no one board has everything we want, so we decided to make our own version that combines all our favorite features. The RedBoard combines the simplicity of the UNO’s Optiboot bootloader (which is used in the Pro series), the stability of the FTDI (which we all missed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
  LCD screen: A standard character display, usually with 2x16 characters. Comes in many colors.
  TSR-3386UT Square Trimming Potentiometer: Trimpot 10K with Knob
