# Fritzing sketch SIK_Circuit_4C_Who_Am_I_Game (saved by Fritzing 0.9.3b)
breadboards: 1

parts:
  Parts1 = SparkFun RedBoard [part_number=DEV-12757]
  LCD2 = LCD screen
  R3 = TSR-3386UT Square Trimming Potentiometer [part_number=TSR-3386]
  SG5 = Buzzer 12mm [package=buzzer-12mm-ns]
  S8 = Pushbutton [part_number=COM-09190 package="[THT]"]

nets:
  N1: Parts1.D8, LCD2.DB7
  N2: Parts1.D9_PWM, LCD2.DB6
  N3: Parts1.D10_PWM/SS, LCD2.DB5
  N4: Parts1.D11_PWM/MOSI, LCD2.DB4
  N5: Parts1.D12/MISO, LCD2.E
  N6: Parts1.D13/SCK, LCD2.RS
  N7: Parts1.D2, S8.Pin_1, S8.Pin_2
  N8: Parts1.D6_PWM, SG5.1
  5V: Parts1.5V, LCD2.VDD, LCD2.LED+, R3.Leg1
  GND: Parts1.GND, LCD2.VSS, LCD2.R/W, LCD2.LED-, R3.Leg2, SG5.2, S8.Pin_3, S8.Pin_4
  N9: LCD2.V0, R3.wiper

custom parts:
  SparkFun RedBoard: At SparkFun we use many Arduinos and we’re always looking for the simplest, most stable one. Each board is a bit different and no one board has everything we want, so we decided to make our own version that combines all our favorite features. The RedBoard combines the simplicity of the UNO’s Optiboot bootloader (which is used in the Pro series), the stability of the FTDI (which we all missed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
  LCD screen: A standard character display, usually with 2x16 characters. Comes in many colors.
  TSR-3386UT Square Trimming Potentiometer: Trimpot 10K with Knob
  Buzzer 12mm: Buzzer 12mm Spark Fun Electronics SKU : Comp-Buzzer Through hole
  Pushbutton: A generic pushbutton. This is a standard 12mm square momentary button. What we really like is the large button head and good tactile feel (it ‘clicks’ really well). This button is great for user input on a PCB or a good, big reset button on a breadboard. Breadboard friendly! SparkFun Storefront SKU: COM-09190 Modified by: Ho Yun "Bobby" Chan @ SparkFun Electronics Inc.
