# Fritzing sketch SIK_Circuit_5A_Motor _Basics (saved by Fritzing 0.9.3b)
breadboards: 1

parts:
  Parts2 = SparkFun RedBoard [part_number=DEV-12757]
  S2 = Toggle Switch [package=THT]
  M4 = DC Motor  # not connected
  Part3 = SparkFun_Motor_Driver-TB6612FNG_v11  # not connected

nets:
  N1: Parts2.D7, S2.L1
  N2: Parts2.GND, S2.COM

custom parts:
  SparkFun RedBoard: At SparkFun we use many Arduinos and we’re always looking for the simplest, most stable one. Each board is a bit different and no one board has everything we want, so we decided to make our own version that combines all our favorite features. The RedBoard combines the simplicity of the UNO’s Optiboot bootloader (which is used in the Pro series), the stability of the FTDI (which we all missed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
