# Fritzing sketch SIK_Circuit_5C_autonomous_robot (saved by Fritzing 0.9.3b)
breadboards: 1

parts:
  Parts2 = SparkFun RedBoard [part_number=DEV-12757]
  S2 = Toggle Switch [package=THT]
  M4 = DC Motor
  M5 = DC Motor
  Part1 = SparkFun Motor Driver TB6612FNG (v11) [part_number=ROB-14451]
  hc-sr4 = hc-sr04

nets:
  N1: Parts2.D8, Part1.BIN1
  N2: Parts2.D9_PWM, Part1.BIN2
  N3: Parts2.D10_PWM/SS, Part1.PWMB
  N4: Parts2.D11_PWM/MOSI, Part1.PWMA
  N5: Parts2.D12/MISO, Part1.AIN2
  N6: Parts2.D13/SCK, Part1.AIN1
  N7: Parts2.D5_PWM, hc-sr4.Echo
  N8: Parts2.D6_PWM, hc-sr4.Trig
  N9: Parts2.D7, S2.L1
  VCC: Parts2.5V, Part1.VCC, Part1.STBY, hc-sr4.VCC
  GND: Parts2.GND, S2.COM, Part1.GND, hc-sr4.GND
  N10: Parts2.VIN, Part1.VM
  N11: M4.pin_1, Part1.A02
  N12: M4.pin_2, Part1.A01
  N13: M5.pin_1, Part1.B02
  N14: M5.pin_2, Part1.B01

custom parts:
  SparkFun RedBoard: At SparkFun we use many Arduinos and we’re always looking for the simplest, most stable one. Each board is a bit different and no one board has everything we want, so we decided to make our own version that combines all our favorite features. The RedBoard combines the simplicity of the UNO’s Optiboot bootloader (which is used in the Pro series), the stability of the FTDI (which we all missed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
  SparkFun Motor Driver TB6612FNG (v11): The TB6612FNG Motor Driver can control up to two DC motors at a constant current of 1.2A (3.2A peak). Two input signals (IN1 and IN2) can be used to control the motor in one of four function modes: CW, CCW, short-brake and stop. The two motor outputs (A and B) can be separately controlled, and the speed of each motor is controlled via a PWM input signal with a frequency up to 100kHz. The STBY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
  hc-sr04: This is a HC-SR04 Distance Sensor
