# Fritzing sketch SIK_Circuit_1C-Photoresistor (saved by Fritzing 0.9.3b)
breadboards: 1

parts:
  R1 = Resistor [tolerance=±5% resistance=330 package=THT]
  S1 = Flipped LED
  R2 = PHOTOCELL [package=photocell-kit]
  R3 = Resistor [tolerance=±5% resistance=10k package=THT]
  DEV-15123 = SparkFun RedBoard Qwiic

nets:
  N1: R1.Pin_0, S1.anode
  N2: R1.Pin_1, DEV-15123.SCK
  N3: S1.cathode, R3.Pin_0, DEV-15123.GND
  N4: R2.P$1, R3.Pin_1, DEV-15123.AD0
  N5: R2.P$2, DEV-15123.5V

custom parts:
  Flipped LED: Flipped version of the default LED
  SparkFun RedBoard Qwiic: At SparkFun we continually like to innovate, update, and improve even when it comes to our very own development boards. We have multiple versions of the SparkFun RedBoard in our catalog but none of them in an R3 form factor with a Qwiic connector on it to make I2C easy... until now! The SparkFun RedBoard Qwiic is an Arduino-compatible development board that uses a few of the features that we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
