# Fritzing sketch SIK_Circuit_2B_trumpet (saved by Fritzing 0.9.3b)
breadboards: 1

parts:
  SG4 = Buzzer 12mm [package=buzzer-12mm-ns]
  R9 = TSR-3386UT Square Trimming Potentiometer [part_number=TSR-3386]
  DEV-15123 = SparkFun RedBoard Qwiic
  S6 = Pushbutton [part_number=PRT-14460 package="[THT]"]
  S7 = Pushbutton [part_number=PRT-14460 package="[THT]"]
  S8 = Pushbutton [part_number=PRT-14460 package="[THT]"]

nets:
  N1: SG4.1, DEV-15123.SS
  N2: SG4.2, R9.Leg2
  N3: R9.wiper, DEV-15123.GND, S6.Pin_1, S6.Pin_2, S7.Pin_1, S7.Pin_2, S8.Pin_1, S8.Pin_2
  N4: DEV-15123.IO2, S8.Pin_3, S8.Pin_4
  N5: DEV-15123.IO3, S7.Pin_3, S7.Pin_4
  N6: DEV-15123.IO4, S6.Pin_3, S6.Pin_4

custom parts:
  Buzzer 12mm: Buzzer 12mm Spark Fun Electronics SKU : Comp-Buzzer Through hole
  TSR-3386UT Square Trimming Potentiometer: Trimpot 10K with Knob
  SparkFun RedBoard Qwiic: At SparkFun we continually like to innovate, update, and improve even when it comes to our very own development boards. We have multiple versions of the SparkFun RedBoard in our catalog but none of them in an R3 form factor with a Qwiic connector on it to make I2C easy... until now! The SparkFun RedBoard Qwiic is an Arduino-compatible development board that uses a few of the features that we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
  Pushbutton: A generic pushbutton. This is a simple 4-pack of multicolor buttons, great for all sorts of projects! Unlike previous iterations of multicolor buttons, this pack’s tactile switches are actually recessed into the housing so they don’t accidentally fall off during use. Each pack comes with one red button, one blue button, one yellow button and one green button. These are the same buttons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
  Pushbutton: A generic pushbutton. This is a simple 4-pack of multicolor buttons, great for all sorts of projects! Unlike previous iterations of multicolor buttons, this pack’s tactile switches are actually recessed into the housing so they don’t accidentally fall off during use. Each pack comes with one red button, one blue button, one yellow button and one green button. These are the same buttons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
  Pushbutton: A generic pushbutton. This is a simple 4-pack of multicolor buttons, great for all sorts of projects! Unlike previous iterations of multicolor buttons, this pack’s tactile switches are actually recessed into the housing so they don’t accidentally fall off during use. Each pack comes with one red button, one blue button, one yellow button and one green button. These are the same buttons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
