# Fritzing sketch SIK_Circuit_3A_Servo_Motors (saved by Fritzing 0.9.3b)
breadboards: 1

parts:
  R9 = TSR-3386UT Square Trimming Potentiometer [part_number=TSR-3386]
  J2 = Basic Servo
  DEV-15123 = SparkFun RedBoard Qwiic

nets:
  GND: R9.Leg1, J2.gnd, DEV-15123.GND
  N1: R9.wiper, DEV-15123.AD0
  VCC: R9.Leg2, J2.vcc, DEV-15123.5V, DEV-15123.IOREF
  N2: J2.pulse, DEV-15123.IO9

custom parts:
  TSR-3386UT Square Trimming Potentiometer: Trimpot 10K with Knob
  SparkFun RedBoard Qwiic: At SparkFun we continually like to innovate, update, and improve even when it comes to our very own development boards. We have multiple versions of the SparkFun RedBoard in our catalog but none of them in an R3 form factor with a Qwiic connector on it to make I2C easy... until now! The SparkFun RedBoard Qwiic is an Arduino-compatible development board that uses a few of the features that we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
