# Fritzing sketch SIK_Circuit_3C_Motion_Alarm (saved by Fritzing 0.9.3b)
breadboards: 1

parts:
  R1 = Resistor [tolerance=±5% resistance=330 package=THT]
  R4 = Resistor [tolerance=±5% resistance=330 package=THT]
  R5 = Resistor [tolerance=±5% resistance=330 package=THT]
  J3 = Basic Servo
  SG5 = Buzzer 12mm [package=buzzer-12mm-ns]
  hc-sr4 = HC-SR04
  DEV-15123 = SparkFun RedBoard Qwiic
  LED1 = RGB LED (com. cathode, rgb) [package="5 mm [THT]"]

nets:
  N1: R1.Pin_0, LED1.blue_anode
  N2: R1.Pin_1, DEV-15123.IO6
  N3: R4.Pin_0, LED1.green_anode
  N4: R4.Pin_1, DEV-15123.IO5
  N5: R5.Pin_0, LED1.red_anode
  N6: R5.Pin_1, DEV-15123.IO3
  GND: J3.gnd, SG5.2, hc-sr4.GND, DEV-15123.GND, LED1.common_cathode
  VCC: J3.vcc, hc-sr4.VCC, DEV-15123.5V
  N7: J3.pulse, DEV-15123.IO9
  N8: SG5.1, DEV-15123.SS
  N9: hc-sr4.Trig, DEV-15123.MOSI
  N10: hc-sr4.Echo, DEV-15123.MISO

custom parts:
  Buzzer 12mm: Buzzer 12mm Spark Fun Electronics SKU : Comp-Buzzer Through hole
  HC-SR04: This is a HC-SR04 Distance Sensor. This economical sensor provides 2cm to 400cm of non-contact measurement functionality with a ranging accuracy that can reach up to 3mm. Each HC-SR04 module includes an ultrasonic transmitter, a receiver and a control circuit. There are only four pins that you need to worry about on the HC-SR04: VCC (Power), Trig (Trigger), Echo (Receive), and GND (Ground).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
  SparkFun RedBoard Qwiic: At SparkFun we continually like to innovate, update, and improve even when it comes to our very own development boards. We have multiple versions of the SparkFun RedBoard in our catalog but none of them in an R3 form factor with a Qwiic connector on it to make I2C easy... until now! The SparkFun RedBoard Qwiic is an Arduino-compatible development board that uses a few of the features that we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
