# Fritzing sketch SIK_Circuit_4A_Hello_World (saved by Fritzing 0.9.3b)
breadboards: 1

parts:
  LCD2 = LCD screen
  R3 = TSR-3386UT Square Trimming Potentiometer [part_number=TSR-3386]
  DEV-15123 = SparkFun RedBoard Qwiic

nets:
  VSS: LCD2.VSS, LCD2.R/W, LCD2.LED-, R3.Leg2, DEV-15123.GND
  VDD: LCD2.VDD, LCD2.LED+, R3.Leg1, DEV-15123.5V, DEV-15123.IOREF
  N1: LCD2.V0, R3.wiper
  N2: LCD2.RS, DEV-15123.SCK
  N3: LCD2.E, DEV-15123.MISO
  N4: LCD2.DB4, DEV-15123.MOSI
  N5: LCD2.DB5, DEV-15123.SS
  N6: LCD2.DB6, DEV-15123.IO9
  N7: LCD2.DB7, DEV-15123.IO8

custom parts:
  LCD screen: A standard character display, usually with 2x16 characters. Comes in many colors.
  TSR-3386UT Square Trimming Potentiometer: Trimpot 10K with Knob
  SparkFun RedBoard Qwiic: At SparkFun we continually like to innovate, update, and improve even when it comes to our very own development boards. We have multiple versions of the SparkFun RedBoard in our catalog but none of them in an R3 form factor with a Qwiic connector on it to make I2C easy... until now! The SparkFun RedBoard Qwiic is an Arduino-compatible development board that uses a few of the features that we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
