# Fritzing sketch SIK_Circuit_4C_Who_Am_I_Game (saved by Fritzing 0.9.3b)
breadboards: 1

parts:
  LCD2 = LCD screen
  R3 = TSR-3386UT Square Trimming Potentiometer [part_number=TSR-3386]
  SG5 = Buzzer 12mm [package=buzzer-12mm-ns]
  DEV-15123 = SparkFun RedBoard Qwiic
  S8 = Pushbutton [part_number=PRT-14460 package="[THT]"]

nets:
  VSS: LCD2.VSS, LCD2.R/W, LCD2.LED-, R3.Leg2, SG5.2, DEV-15123.GND, S8.Pin_3, S8.Pin_4
  VDD: LCD2.VDD, LCD2.LED+, R3.Leg1, DEV-15123.5V, DEV-15123.IOREF
  N1: LCD2.V0, R3.wiper
  N2: LCD2.RS, DEV-15123.SCK
  N3: LCD2.E, DEV-15123.MISO
  N4: LCD2.DB4, DEV-15123.MOSI
  N5: LCD2.DB5, DEV-15123.SS
  N6: LCD2.DB6, DEV-15123.IO9
  N7: LCD2.DB7, DEV-15123.IO8
  N8: SG5.1, DEV-15123.IO6
  N9: DEV-15123.IO2, S8.Pin_1, S8.Pin_2

custom parts:
  LCD screen: A standard character display, usually with 2x16 characters. Comes in many colors.
  TSR-3386UT Square Trimming Potentiometer: Trimpot 10K with Knob
  Buzzer 12mm: Buzzer 12mm Spark Fun Electronics SKU : Comp-Buzzer Through hole
  SparkFun RedBoard Qwiic: At SparkFun we continually like to innovate, update, and improve even when it comes to our very own development boards. We have multiple versions of the SparkFun RedBoard in our catalog but none of them in an R3 form factor with a Qwiic connector on it to make I2C easy... until now! The SparkFun RedBoard Qwiic is an Arduino-compatible development board that uses a few of the features that we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
  Pushbutton: A generic pushbutton. This is a simple 4-pack of multicolor buttons, great for all sorts of projects! Unlike previous iterations of multicolor buttons, this pack’s tactile switches are actually recessed into the housing so they don’t accidentally fall off during use. Each pack comes with one red button, one blue button, one yellow button and one green button. These are the same buttons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
