# Fritzing sketch SIK_Circuit_5B_Remote-Controlled_Robot (saved by Fritzing 0.9.3b)
breadboards: 1

parts:
  S2 = Toggle Switch [package=THT]
  Part1 = SparkFun Motor Driver TB6612FNG (v11) [part_number=ROB-14451]
  M6 = DC Motor
  M7 = DC Motor
  DEV-15123 = SparkFun RedBoard Qwiic

nets:
  N1: S2.L1, DEV-15123.IO7
  GND: S2.COM, Part1.GND, DEV-15123.GND
  N2: Part1.B01, M6.pin_2
  N3: Part1.B02, M6.pin_1
  N4: Part1.A02, M7.pin_1
  N5: Part1.A01, M7.pin_2
  VCC: Part1.VCC, Part1.STBY, DEV-15123.5V
  N6: Part1.VM, DEV-15123.VIN
  N7: Part1.PWMA, DEV-15123.MOSI
  N8: Part1.AIN2, DEV-15123.MISO
  N9: Part1.AIN1, DEV-15123.SCK
  N10: Part1.BIN1, DEV-15123.IO8
  N11: Part1.BIN2, DEV-15123.IO9
  N12: Part1.PWMB, DEV-15123.SS

custom parts:
  SparkFun Motor Driver TB6612FNG (v11): The TB6612FNG Motor Driver can control up to two DC motors at a constant current of 1.2A (3.2A peak). Two input signals (IN1 and IN2) can be used to control the motor in one of four function modes: CW, CCW, short-brake and stop. The two motor outputs (A and B) can be separately controlled, and the speed of each motor is controlled via a PWM input signal with a frequency up to 100kHz. The STBY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
  DC Motor: Your standard DC Motor
  SparkFun RedBoard Qwiic: At SparkFun we continually like to innovate, update, and improve even when it comes to our very own development boards. We have multiple versions of the SparkFun RedBoard in our catalog but none of them in an R3 form factor with a Qwiic connector on it to make I2C easy... until now! The SparkFun RedBoard Qwiic is an Arduino-compatible development board that uses a few of the features that we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
