# Fritzing sketch SIK_Circuit_1D-RGBNightlight (saved by Fritzing 0.9.3b)
breadboards: 1

parts:
  R1 = Resistor [tolerance=±5% resistance=330 package=THT]
  R2 = PHOTOCELL [package=photocell-kit]
  R3 = Resistor [tolerance=±5% resistance=10k package=THT]
  R4 = Resistor [tolerance=±5% resistance=330 package=THT]
  R5 = Resistor [tolerance=±5% resistance=330 package=THT]
  R10 = TSR-3386UT Square Trimming Potentiometer [part_number=TSR-3386]
  DEV-15123 = SparkFun RedBoard Qwiic
  LED1 = RGB LED (com. cathode, rgb) [package="5 mm [THT]"]

nets:
  N1: R1.Pin_0, LED1.blue_anode
  N2: R1.Pin_1, DEV-15123.MOSI
  N3: R2.P$1, R3.Pin_1, DEV-15123.AD0
  N4: R2.P$2, R10.Leg2, DEV-15123.5V
  N5: R3.Pin_0, R10.Leg1, DEV-15123.GND, LED1.common_cathode
  N6: R4.Pin_0, LED1.green_anode
  N7: R4.Pin_1, DEV-15123.SS
  N8: R5.Pin_0, LED1.red_anode
  N9: R5.Pin_1, DEV-15123.IO9
  N10: R10.wiper, DEV-15123.AD1

custom parts:
  TSR-3386UT Square Trimming Potentiometer: Trimpot 10K with Knob
  SparkFun RedBoard Qwiic: At SparkFun we continually like to innovate, update, and improve even when it comes to our very own development boards. We have multiple versions of the SparkFun RedBoard in our catalog but none of them in an R3 form factor with a Qwiic connector on it to make I2C easy... until now! The SparkFun RedBoard Qwiic is an Arduino-compatible development board that uses a few of the features that we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
