# Fritzing sketch SIK_Circuit_2A_buzzer (saved by Fritzing 0.9.3b)
breadboards: 1

parts:
  SG4 = Buzzer 12mm [package=buzzer-12mm-ns]
  R9 = TSR-3386UT Square Trimming Potentiometer [part_number=TSR-3386]
  DEV-15123 = SparkFun RedBoard Qwiic

nets:
  N1: SG4.1, DEV-15123.SS
  N2: SG4.2, R9.Leg2
  N3: R9.wiper, DEV-15123.GND

custom parts:
  Buzzer 12mm: Buzzer 12mm Spark Fun Electronics SKU : Comp-Buzzer Through hole
  TSR-3386UT Square Trimming Potentiometer: Trimpot 10K with Knob
  SparkFun RedBoard Qwiic: At SparkFun we continually like to innovate, update, and improve even when it comes to our very own development boards. We have multiple versions of the SparkFun RedBoard in our catalog but none of them in an R3 form factor with a Qwiic connector on it to make I2C easy... until now! The SparkFun RedBoard Qwiic is an Arduino-compatible development board that uses a few of the features that we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
