# Fritzing sketch SIK_Circuit_2C_SimonSays (saved by Fritzing 0.9.3b)
breadboards: 1

parts:
  SG4 = Buzzer 12mm [package=buzzer-12mm-ns]
  R9 = TSR-3386UT Square Trimming Potentiometer [part_number=TSR-3386]
  LED1 = LED - 5mm [color="Blue (470nm)" package="5 mm [THT]"]
  LED2 = LED - 5mm [color="Green (555nm)" package="5 mm [THT]"]
  LED4 = LED - 5mm [color="Red (633nm)" package="5 mm [THT]"]
  R10 = Resistor [tolerance=±5% resistance=330 package=THT]
  R11 = Resistor [tolerance=±5% resistance=330 package=THT]
  R12 = Resistor [tolerance=±5% resistance=330 package=THT]
  R13 = Resistor [tolerance=±5% resistance=330 package=THT]
  DEV-15123 = SparkFun RedBoard Qwiic
  S7 = Pushbutton [part_number=PRT-14460 package="[THT]"]
  S8 = Pushbutton [part_number=PRT-14460 package="[THT]"]
  S9 = Pushbutton [part_number=PRT-14460 package="[THT]"]
  S10 = Pushbutton [part_number=PRT-14460 package="[THT]"]
  LED5 = LED - 5mm [color="Yellow (595nm)" package="5 mm [THT]"]

nets:
  N1: SG4.1, DEV-15123.SS
  N2: SG4.2, R9.Leg2
  N3: R9.wiper, R10.Pin_1, R11.Pin_1, R12.Pin_1, R13.Pin_1, DEV-15123.GND, S7.Pin_1, S7.Pin_2, S8.Pin_1, S8.Pin_2, S9.Pin_1, S9.Pin_2, S10.Pin_1, S10.Pin_2
  N4: LED1.cathode, R13.Pin_0
  N5: LED1.anode, DEV-15123.IO9
  N6: LED2.cathode, R12.Pin_0
  N7: LED2.anode, DEV-15123.IO7
  N8: LED4.cathode, R10.Pin_0
  N9: LED4.anode, DEV-15123.IO3
  N10: R11.Pin_0, LED5.cathode
  N11: DEV-15123.IO8, S7.Pin_3, S7.Pin_4
  N12: DEV-15123.IO2, S9.Pin_3, S9.Pin_4
  N13: DEV-15123.IO4, S8.Pin_3, S8.Pin_4
  N14: DEV-15123.IO5, LED5.anode
  N15: DEV-15123.IO6, S10.Pin_3, S10.Pin_4

custom parts:
  Buzzer 12mm: Buzzer 12mm Spark Fun Electronics SKU : Comp-Buzzer Through hole
  TSR-3386UT Square Trimming Potentiometer: Trimpot 10K with Knob
  SparkFun RedBoard Qwiic: At SparkFun we continually like to innovate, update, and improve even when it comes to our very own development boards. We have multiple versions of the SparkFun RedBoard in our catalog but none of them in an R3 form factor with a Qwiic connector on it to make I2C easy... until now! The SparkFun RedBoard Qwiic is an Arduino-compatible development board that uses a few of the features that we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
  Pushbutton: A generic pushbutton. This is a simple 4-pack of multicolor buttons, great for all sorts of projects! Unlike previous iterations of multicolor buttons, this pack’s tactile switches are actually recessed into the housing so they don’t accidentally fall off during use. Each pack comes with one red button, one blue button, one yellow button and one green button. These are the same buttons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
  Pushbutton: A generic pushbutton. This is a simple 4-pack of multicolor buttons, great for all sorts of projects! Unlike previous iterations of multicolor buttons, this pack’s tactile switches are actually recessed into the housing so they don’t accidentally fall off during use. Each pack comes with one red button, one blue button, one yellow button and one green button. These are the same buttons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
  Pushbutton: A generic pushbutton. This is a simple 4-pack of multicolor buttons, great for all sorts of projects! Unlike previous iterations of multicolor buttons, this pack’s tactile switches are actually recessed into the housing so they don’t accidentally fall off during use. Each pack comes with one red button, one blue button, one yellow button and one green button. These are the same buttons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
  Pushbutton: A generic pushbutton. This is a simple 4-pack of multicolor buttons, great for all sorts of projects! Unlike previous iterations of multicolor buttons, this pack’s tactile switches are actually recessed into the housing so they don’t accidentally fall off during use. Each pack comes with one red button, one blue button, one yellow button and one green button. These are the same buttons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
