# Fritzing sketch 12942_sfe_Bus_Pirate_v3.6a (saved by Fritzing 0.9.2b)

parts:
  Breakout_Board1 = Bus Pirate [package="DIP (Dual Inline) [THT]"]
  IC1 = SparkFun LSM303C 6 DOF IMU Breakout [chip_label=IC package="DIP (Dual Inline) [THT]"]

nets:
  N1: Breakout_Board1.OE_LV, IC1.pin1
  N2: Breakout_Board1.A1, IC1.pin2
  N3: Breakout_Board1.GND_A, IC1.pin4
  N4: Breakout_Board1.pin_7, IC1.pin3

custom parts:
  Bus Pirate: Breakout board for the TI TXB0104 bi-directional level shifter IC. VccA should be lower than VccB. VccA can range from 1.2V to 3.6V, and VCCB can range from 1.65V to 5.5V.
  SparkFun LSM303C 6 DOF IMU Breakout: A DIP stand-in part for whatever IC you want. With 12 pins on a 300mil dual inline package (DIP) footprint.
