# Fritzing sketch 13743_sfe_shifting_microsd (saved by Fritzing 0.9.2b)

parts:
  Breakout_Board1 = Level Shifting uSD Breakout [package="DIP (Dual Inline) [THT]"]
  Parts1 = SparkFun RedBoard [part_number=DEV-12757]

nets:
  N1: Breakout_Board1.OE_LV, Parts1.5V
  N2: Breakout_Board1.A1, Parts1.D8
  N3: Breakout_Board1.A2, Parts1.D11_PWM/MOSI
  N4: Breakout_Board1.A3, Parts1.D13/SCK
  N5: Breakout_Board1.A4, Parts1.D12/MISO
  N6: Breakout_Board1.VccA, Parts1.D9_PWM
  N7: Breakout_Board1.GND_A, Parts1.GND

custom parts:
  Level Shifting uSD Breakout: Breakout board for the TI TXB0104 bi-directional level shifter IC. VccA should be lower than VccB. VccA can range from 1.2V to 3.6V, and VCCB can range from 1.65V to 5.5V.
  SparkFun RedBoard: At SparkFun we use many Arduinos and we’re always looking for the simplest, most stable one. Each board is a bit different and no one board has everything we want, so we decided to make our own version that combines all our favorite features. The RedBoard combines the simplicity of the UNO’s Optiboot bootloader (which is used in the Pro series), the stability of the FTDI (which we all missed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
